// Logisim project 8_BIT_ALU_INTEGRATED WITH ALL REGISTER FILE.circ as structural Verilog: 5 circuits, main circuit ALU
module ALU (
  input  [7:0] B,
  input  [7:0] A,
  input  [3:0] opcode,
  input  [2:0] SHIFT_BITS,
  output [15:0] DATA_OUTPUT
);

  wire adder_1_cout, subtractor_1_bout;
  wire [7:0] adder_1_out, and_1_out, bit_extender_8_out, bit_extender_9_out, divider_1_out, divider_1_rem,
       multiplier_1_cout, multiplier_1_out, nand_1_out, nor_1_out, not_1_out, not_2_out, or_1_out,
       shifter_1_out, shifter_2_out, shifter_3_out, shifter_4_out, subtractor_1_out, xor_1_out;
  wire [15:0] bit_extender_1_out, bit_extender_2_out, bit_extender_3_out, bit_extender_4_out,
       bit_extender_5_out, bit_extender_6_out, bit_extender_7_out, bit_extender_10_out, bit_extender_11_out,
       bit_extender_12_out, bit_extender_13_out;

  assign not_1_out = ~A;  // NOT_Gate not_1, 8 bits wide
  assign not_2_out = ~B;  // NOT_Gate not_2, 8 bits wide
  assign and_1_out = B & A;  // AND_Gate and_1, 8 bits wide
  assign or_1_out = B | A;  // OR_Gate or_1, 8 bits wide
  assign nand_1_out = ~(B & A);  // NAND_Gate nand_1, 8 bits wide
  assign nor_1_out = ~(B | A);  // NOR_Gate nor_1, 8 bits wide
  assign xor_1_out = B ^ A;  // XOR_Gate xor_1, 8 bits wide
  Adder adder_1 (.a(B), .b(A), .out(adder_1_out), .cout(adder_1_cout));  // open: cin
  Subtractor subtractor_1 (.a(B), .b(A), .out(subtractor_1_out), .bout(subtractor_1_bout));  // open: bin
  Multiplier multiplier_1 (.a(B), .b(A), .out(multiplier_1_out), .cout(multiplier_1_cout));  // open: cin
  Divider divider_1 (.a(B), .b(A), .out(divider_1_out), .rem(divider_1_rem));  // open: upper
  Shifter shifter_1 (.in(A), .\dist (SHIFT_BITS), .out(shifter_1_out));
  Shifter #(.shift("lr")) shifter_2 (.in(A), .\dist (SHIFT_BITS), .out(shifter_2_out));
  Shifter #(.shift("rr")) shifter_3 (.in(A), .\dist (SHIFT_BITS), .out(shifter_3_out));
  Shifter #(.shift("rl")) shifter_4 (.in(A), .\dist (SHIFT_BITS), .out(shifter_4_out));
  assign bit_extender_1_out = {{8{1'b0}}, not_1_out};  // Bit_Extender bit_extender_1
  assign bit_extender_2_out = {{8{1'b0}}, not_2_out};  // Bit_Extender bit_extender_2
  assign bit_extender_3_out = {{8{1'b0}}, and_1_out};  // Bit_Extender bit_extender_3
  assign bit_extender_4_out = {{8{1'b0}}, or_1_out};  // Bit_Extender bit_extender_4
  assign bit_extender_5_out = {{8{1'b0}}, nand_1_out};  // Bit_Extender bit_extender_5
  assign bit_extender_6_out = {{8{1'b0}}, nor_1_out};  // Bit_Extender bit_extender_6
  assign bit_extender_7_out = {{8{1'b0}}, xor_1_out};  // Bit_Extender bit_extender_7
  assign bit_extender_8_out = {{7{1'b0}}, adder_1_cout};  // Bit_Extender bit_extender_8
  assign bit_extender_9_out = {{7{1'b0}}, subtractor_1_bout};  // Bit_Extender bit_extender_9
  assign bit_extender_10_out = {{8{1'b0}}, shifter_1_out};  // Bit_Extender bit_extender_10
  assign bit_extender_11_out = {{8{1'b0}}, shifter_2_out};  // Bit_Extender bit_extender_11
  assign bit_extender_12_out = {{8{1'b0}}, shifter_3_out};  // Bit_Extender bit_extender_12
  assign bit_extender_13_out = {{8{1'b0}}, shifter_4_out};  // Bit_Extender bit_extender_13
  Multiplexer #(.select(4), .width(16), .enable("false")) multiplexer_1 (
    .in0(bit_extender_1_out), .in1(bit_extender_2_out), .in2(bit_extender_3_out), .in3(bit_extender_4_out),
    .in4(bit_extender_5_out), .in5(bit_extender_6_out), .in6(bit_extender_7_out),
    .in7({bit_extender_8_out, adder_1_out}), .in8({bit_extender_9_out, subtractor_1_out}),
    .in9({multiplier_1_cout, multiplier_1_out}), .in10({divider_1_rem, divider_1_out}),
    .in11(bit_extender_10_out), .in12(bit_extender_11_out), .in13(bit_extender_12_out),
    .in14(bit_extender_13_out), .out(DATA_OUTPUT), .sel(opcode));  // open: in15
endmodule

module Registry (
  input  [7:0] DATA_IN,
  input  CLOCK,
  input  [3:0] RX,
  input  R_W_prime,
  output [7:0] RESULT
);

  wire decoder_1_out0, decoder_1_out1, decoder_1_out2, decoder_1_out3, decoder_1_out4, decoder_1_out5,
       decoder_1_out6, decoder_1_out7, decoder_1_out8, decoder_1_out9, decoder_1_out10, decoder_1_out11,
       decoder_1_out12, decoder_1_out13, decoder_1_out14, decoder_1_out15, not_1_out;
  wire [7:0] register_1_q, register_2_q, register_3_q, register_4_q, register_5_q, register_6_q,
       register_7_q, register_8_q, register_9_q, register_10_q, register_11_q, register_12_q, register_13_q,
       register_14_q, register_15_q, register_16_q;

  not not_1 (not_1_out, R_W_prime);
  Decoder #(.select(4), .disabled(0)) decoder_1 (
    .out0(decoder_1_out0), .out1(decoder_1_out1), .out2(decoder_1_out2), .out3(decoder_1_out3),
    .out4(decoder_1_out4), .out5(decoder_1_out5), .out6(decoder_1_out6), .out7(decoder_1_out7),
    .out8(decoder_1_out8), .out9(decoder_1_out9), .out10(decoder_1_out10), .out11(decoder_1_out11),
    .out12(decoder_1_out12), .out13(decoder_1_out13), .out14(decoder_1_out14), .out15(decoder_1_out15),
    .sel(RX), .en(not_1_out));
  Register register_1 (.D(DATA_IN), .en(decoder_1_out0), .Q(register_1_q), .clk(CLOCK));  // open: clr
  Register register_2 (.D(DATA_IN), .en(decoder_1_out1), .Q(register_2_q), .clk(CLOCK));  // open: clr
  Register register_3 (.D(DATA_IN), .en(decoder_1_out2), .Q(register_3_q), .clk(CLOCK));  // open: clr
  Register register_4 (.D(DATA_IN), .en(decoder_1_out3), .Q(register_4_q), .clk(CLOCK));  // open: clr
  Register register_5 (.D(DATA_IN), .en(decoder_1_out4), .Q(register_5_q), .clk(CLOCK));  // open: clr
  Register register_6 (.D(DATA_IN), .Q(register_6_q), .clk(CLOCK));  // open: en, clr
  Register register_7 (.D(DATA_IN), .Q(register_7_q), .clk(CLOCK));  // open: en, clr
  Register register_8 (.D(DATA_IN), .Q(register_8_q), .clk(CLOCK));  // open: en, clr
  Register register_9 (.D(DATA_IN), .Q(register_9_q), .clk(CLOCK));  // open: en, clr
  Register register_10 (.D(DATA_IN), .Q(register_10_q), .clk(CLOCK));  // open: en, clr
  Register register_11 (.D(DATA_IN), .Q(register_11_q), .clk(CLOCK));  // open: en, clr
  Register register_12 (.D(DATA_IN), .Q(register_12_q), .clk(CLOCK));  // open: en, clr
  Register register_13 (.D(DATA_IN), .Q(register_13_q), .clk(CLOCK));  // open: en, clr
  Register register_14 (.D(DATA_IN), .Q(register_14_q), .clk(CLOCK));  // open: en, clr
  Register register_15 (.D(DATA_IN), .Q(register_15_q), .clk(CLOCK));  // open: en, clr
  Register register_16 (.D(DATA_IN), .Q(register_16_q), .clk(CLOCK));  // open: en, clr
  Multiplexer #(.select(4), .width(8), .disabled(0)) multiplexer_1 (
    .in0(register_1_q), .in1(register_2_q), .in2(register_3_q), .in3(register_4_q), .in4(register_5_q),
    .in5(register_6_q), .in6(register_7_q), .in7(register_8_q), .in8(register_9_q), .in9(register_10_q),
    .in10(register_11_q), .in11(register_12_q), .in12(register_13_q), .in13(register_14_q),
    .in14(register_15_q), .in15(register_16_q), .out(RESULT), .sel(RX), .en(R_W_prime));
  Hex_Digit_Display hex_digit_display_1 (.value(RESULT[3:0]));  // open: dp
  Hex_Digit_Display hex_digit_display_2 (.value(RESULT[7:4]));  // open: dp

  // Other names for the same wires on the sheet: D[7:0] = DATA_IN
endmodule

module Memory (
  input  R_W_prime,
  input  [7:0] ADDRESS,
  input  [7:0] DATA,
  output [7:0] OUTPUT
);

  wire CLOCK_out, not_1_out;

  Clock CLOCK (.out(CLOCK_out));
  not not_1 (not_1_out, R_W_prime);
  RAM #(.bus("separate")) ram_1 (
    .addr(ADDRESS), .din(DATA), .data(OUTPUT), .str(not_1_out), .clk(CLOCK_out), .ld(R_W_prime));  // open: sel, clr

  // Notes on the sheet:
  //   256X8
endmodule

module Processor (
  input  [3:0] in_1,
  input  enable,
  input  clock,
  input  reset,
  input  [7:0] in_5,
  input  R_W_prime,
  input  [7:0] in_7,
  output [7:0] out_8,
  output [15:0] out_9,
  output [7:0] out_10
);

  wire not_1_out, undriven;
  wire [7:0] PC_result;
  wire [15:0] rom_1_data;

  PC PC (.address(8'h1), .enable(enable), .clock(clock), .reset(reset), .result(PC_result));
  ROM #(.dataWidth(16)) rom_1 (.addr(PC_result), .data(rom_1_data));  // open: sel
  not not_1 (not_1_out, R_W_prime);
  Registry REGISTER (.DATA_IN(in_5), .CLOCK(undriven), .RX(rom_1_data[11:8]), .R_W_prime(R_W_prime), .RESULT(out_8));
  ALU ALU (.B(out_10), .A(out_8), .opcode(rom_1_data[15:12]), .DATA_OUTPUT(out_9));  // open: SHIFT_BITS
  RAM #(.bus("separate")) ram_1 (
    .addr(rom_1_data[7:0]), .din(in_7), .data(out_10), .str(not_1_out), .clk(undriven), .ld(R_W_prime));  // open: sel, clr

  // Notes on the sheet:
  //   0000- NOT A
  //   0001- NOT B
  //   0010- AND
  //   0011- OR
  //   0100- NAND
  //   0101- NOR
  //   contents of rom_1 (hex, n*v repeats v):
  //   7001 9202 a310
  //   0111- ADDER
  //   1000- SUBTRACTOR
  //   1001- MULTIPLIER
  //   1010- DIVIDER
  //   1011- SHIFT LEFT
  //   1100- SHIFT RIGHT
  //   1101- ROTATE LEFT
  //   1110- ROTATE RIGHT
endmodule

module PC (
  input  [7:0] address,
  input  enable,
  input  clock,
  input  reset,
  output [7:0] result
);

  wire [7:0] adder_1_out;

  Adder adder_1 (.a(address), .b(result), .out(adder_1_out));  // open: cin, cout
  Register register_1 (.D(adder_1_out), .en(enable), .Q(result), .clk(clock), .clr(reset));
endmodule
